// Logisim project SAP_1_Project.circ as structural Verilog: 14 circuits, main circuit main
module main (
  input  [3:0] in_1,
  input  in_2,
  output [3:0] out_3,
  output [3:0] out_4,
  output HLT,
  output CP,
  output EP,
  output nLM,
  output nCE,
  output nLi,
  output nEi,
  output nLa,
  output EA,
  output SU,
  output EU,
  output nLb,
  output nLo
);

  wire clock_1_out, controlled_buffer_2_out, not_1_out, not_2_out, not_3_out, not_4_out, not_5_out,
       not_6_out, not_7_out, not_8_out, not_9_out;
  wire [3:0] A_Register_output, A_Register_output_2, ir_1_output0_3, ir_1_output4_7, mar_1_output;
  wire [7:0] B_Register_output, Output_Register_output, xor_7_out;

  not not_1 (not_1_out, controlled_buffer_2_out);
  not not_2 (not_2_out, nLM);
  not not_3 (not_3_out, nCE);
  not not_4 (not_4_out, nLi);
  pc pc_1 (.Output(out_4), .Cp(CP), .CLK(not_1_out), .CLR(in_2), .Ep(EP));
  mar mar_1 (
    .INPUT(out_4), .OUTPUT(mar_1_output), .LOAD(not_2_out), .CLK(controlled_buffer_2_out), .CLR(in_2),
    .ENABLE(1'b1));
  IR ir_1 (
    .LOAD(not_4_out), .CLK(controlled_buffer_2_out), .INPUT({out_3, out_4}), .OUTPUT4_7(ir_1_output4_7),
    .OUTPUT0_3(ir_1_output0_3), .ENABLE(1'b1), .CLR(in_2));
  RAM #(.addrWidth(4)) ram_1 (.addr(mar_1_output), .data({out_3, out_4}), .ld(not_3_out));  // open: sel, clk, clr
  assign out_4 = not_5_out ? ir_1_output0_3 : 4'bz;  // Controlled_Buffer controlled_buffer_1
  not not_5 (not_5_out, nEi);
  Controller_Sequencer controller_sequencer_1 (
    .CLR(in_2), .I7_I4(ir_1_output4_7), .HLT(HLT), .CP(CP), .EP(EP), .nLM(nLM), .nCE(nCE), .nLI(nLi),
    .nEI(nEi), .nLA(nLa), .EA(EA), .SU(SU), .EU(EU), .nLB(nLb), .nLO(nLo), .CLK(controlled_buffer_2_out));
  Clock clock_1 (.out(clock_1_out));
  assign controlled_buffer_2_out = not_6_out ? clock_1_out : 1'bz;  // Controlled_Buffer controlled_buffer_2
  not not_6 (not_6_out, HLT);
  assign {out_3, out_4} = EA ? {A_Register_output_2, A_Register_output} : 8'bz;  // Controlled_Buffer controlled_buffer_3
  Accmulator A_Register (
    .ENABLE(1'b1), .CLK(controlled_buffer_2_out), .OUTPUT({A_Register_output_2, A_Register_output}),
    .nLA(not_7_out), .INPUT({out_3, out_4}));
  xor xor_1 (xor_7_out[6], SU, B_Register_output[6]);
  xor xor_2 (xor_7_out[7], SU, B_Register_output[7]);
  not not_7 (not_7_out, nLa);
  Adder_Subtractor Adder_Subtractor (
    .A({A_Register_output_2, A_Register_output}), .B(xor_7_out), .Cin(SU), .OUTPUT({out_3, out_4}), .EU(EU));  // open: Cout
  xor xor_3 (xor_7_out[4], SU, B_Register_output[4]);
  xor xor_4 (xor_7_out[5], SU, B_Register_output[5]);
  xor xor_5 (xor_7_out[3], SU, B_Register_output[3]);
  xor xor_6 (xor_7_out[2], SU, B_Register_output[2]);
  not not_8 (not_8_out, nLb);
  B_Register B_Register (
    .CLK(controlled_buffer_2_out), .OUTPUT(B_Register_output), .nLB(not_8_out), .INPUT({out_3, out_4}));
  Output_Register Output_Register (
    .CLK(controlled_buffer_2_out), .OUTPUT(Output_Register_output), .nLO(not_9_out), .INPUT({out_3, out_4}));
  Hex_Digit_Display hex_digit_display_1 (.value(A_Register_output));  // open: dp
  Hex_Digit_Display hex_digit_display_2 (.value(A_Register_output_2));  // open: dp
  xor xor_7 (xor_7_out[0], SU, B_Register_output[0]);
  xor xor_8 (xor_7_out[1], SU, B_Register_output[1]);
  not not_9 (not_9_out, nLo);
  Hex_Digit_Display hex_digit_display_3 (.value(Output_Register_output[7:4]));  // open: dp
  Hex_Digit_Display hex_digit_display_4 (.value(B_Register_output[3:0]));  // open: dp
  Hex_Digit_Display hex_digit_display_5 (.value(B_Register_output[7:4]));  // open: dp
  Hex_Digit_Display hex_digit_display_6 (.value(Output_Register_output[3:0]));  // open: dp

  // Notes on the sheet:
  //   1607061 & 1607100
endmodule

// AC
module Accmulator (
  input  nLA,
  input  [7:0] INPUT,
  input  ENABLE,
  input  CLK,
  output [7:0] OUTPUT
);

  wire and_1_out, and_2_out, and_3_out, and_4_out, and_5_out, and_6_out, and_7_out, and_8_out, and_9_out,
       and_10_out, and_11_out, and_12_out, and_13_out, and_14_out, and_15_out, and_16_out, d_ff_1_q,
       d_ff_2_q, d_ff_3_q, d_ff_4_q, d_ff_5_q, d_ff_6_q, d_ff_7_q, d_ff_8_q, not_1_out, or_1_out, or_2_out,
       or_3_out, or_4_out, or_5_out, or_6_out, or_7_out, or_8_out;

  and and_1 (and_1_out, not_1_out, d_ff_1_q);
  and and_2 (and_2_out, nLA, INPUT[7]);
  or or_1 (or_1_out, and_2_out, and_1_out);
  D_Flip_Flop d_ff_1 (.clk(CLK), .D(or_1_out), .Q(d_ff_1_q));  // open: Qn, preset, en, reset
  assign OUTPUT[7] = ENABLE ? d_ff_1_q : 1'bz;  // Controlled_Buffer controlled_buffer_1
  and and_3 (and_3_out, not_1_out, d_ff_2_q);
  and and_4 (and_4_out, nLA, INPUT[6]);
  or or_2 (or_2_out, and_4_out, and_3_out);
  D_Flip_Flop d_ff_2 (.clk(CLK), .D(or_2_out), .Q(d_ff_2_q));  // open: Qn, preset, en, reset
  assign OUTPUT[6] = ENABLE ? d_ff_2_q : 1'bz;  // Controlled_Buffer controlled_buffer_2
  and and_5 (and_5_out, nLA, INPUT[5]);
  or or_3 (or_3_out, and_5_out, and_6_out);
  and and_6 (and_6_out, not_1_out, d_ff_3_q);
  D_Flip_Flop d_ff_3 (.clk(CLK), .D(or_3_out), .Q(d_ff_3_q));  // open: Qn, preset, en, reset
  assign OUTPUT[5] = ENABLE ? d_ff_3_q : 1'bz;  // Controlled_Buffer controlled_buffer_3
  and and_7 (and_7_out, nLA, INPUT[4]);
  or or_4 (or_4_out, and_7_out, and_8_out);
  and and_8 (and_8_out, not_1_out, d_ff_4_q);
  D_Flip_Flop d_ff_4 (.clk(CLK), .D(or_4_out), .Q(d_ff_4_q));  // open: Qn, preset, en, reset
  and and_9 (and_9_out, nLA, INPUT[3]);
  or or_5 (or_5_out, and_9_out, and_10_out);
  assign OUTPUT[4] = ENABLE ? d_ff_4_q : 1'bz;  // Controlled_Buffer controlled_buffer_4
  and and_10 (and_10_out, not_1_out, d_ff_5_q);
  D_Flip_Flop d_ff_5 (.clk(CLK), .D(or_5_out), .Q(d_ff_5_q));  // open: Qn, preset, en, reset
  and and_11 (and_11_out, nLA, INPUT[2]);
  assign OUTPUT[3] = ENABLE ? d_ff_5_q : 1'bz;  // Controlled_Buffer controlled_buffer_5
  and and_12 (and_12_out, not_1_out, d_ff_6_q);
  or or_6 (or_6_out, and_11_out, and_12_out);
  D_Flip_Flop d_ff_6 (.clk(CLK), .D(or_6_out), .Q(d_ff_6_q));  // open: Qn, preset, en, reset
  assign OUTPUT[2] = ENABLE ? d_ff_6_q : 1'bz;  // Controlled_Buffer controlled_buffer_6
  and and_13 (and_13_out, not_1_out, d_ff_7_q);
  and and_14 (and_14_out, nLA, INPUT[1]);
  or or_7 (or_7_out, and_14_out, and_13_out);
  D_Flip_Flop d_ff_7 (.clk(CLK), .D(or_7_out), .Q(d_ff_7_q));  // open: Qn, preset, en, reset
  assign OUTPUT[1] = ENABLE ? d_ff_7_q : 1'bz;  // Controlled_Buffer controlled_buffer_7
  and and_15 (and_15_out, not_1_out, d_ff_8_q);
  and and_16 (and_16_out, nLA, INPUT[0]);
  or or_8 (or_8_out, and_16_out, and_15_out);
  not not_1 (not_1_out, nLA);
  D_Flip_Flop d_ff_8 (.clk(CLK), .D(or_8_out), .Q(d_ff_8_q));  // open: Qn, preset, en, reset
  assign OUTPUT[0] = ENABLE ? d_ff_8_q : 1'bz;  // Controlled_Buffer controlled_buffer_8

  // Notes on the sheet:
  //   1607100
  //   A Register
endmodule

module FA (
  input  A,
  input  B,
  input  Cin,
  output S,
  output Cout
);

  wire and_1_out, and_2_out, xor_1_out;

  xor xor_1 (xor_1_out, A, B);
  xor xor_2 (S, xor_1_out, Cin);
  and and_1 (and_1_out, Cin, xor_1_out);
  and and_2 (and_2_out, B, A);
  or or_1 (Cout, and_1_out, and_2_out);

  // Notes on the sheet:
  //   1607100
endmodule

// A/S
module Adder_Subtractor (
  input  [7:0] A,
  input  [7:0] B,
  input  Cin,
  input  EU,
  output Cout,
  output [7:0] OUTPUT
);

  wire fa_1_cout, fa_2_cout, fa_3_cout, fa_4_cout, fa_5_cout, fa_6_cout, fa_7_cout;
  wire [7:0] fa_1_s;

  assign OUTPUT = EU ? fa_1_s : 8'bz;  // Controlled_Buffer controlled_buffer_1
  FA fa_1 (.A(A[0]), .B(B[0]), .Cin(Cin), .S(fa_1_s[0]), .Cout(fa_1_cout));
  FA fa_2 (.A(A[1]), .B(B[1]), .Cin(fa_1_cout), .S(fa_1_s[1]), .Cout(fa_2_cout));
  FA fa_3 (.A(A[2]), .B(B[2]), .Cin(fa_2_cout), .S(fa_1_s[2]), .Cout(fa_3_cout));
  FA fa_4 (.A(A[3]), .B(B[3]), .Cin(fa_3_cout), .S(fa_1_s[3]), .Cout(fa_4_cout));
  FA fa_5 (.A(A[4]), .B(B[4]), .Cin(fa_4_cout), .S(fa_1_s[4]), .Cout(fa_5_cout));
  FA fa_6 (.A(A[5]), .B(B[5]), .Cin(fa_5_cout), .S(fa_1_s[5]), .Cout(fa_6_cout));
  FA fa_7 (.A(A[6]), .B(B[6]), .Cin(fa_6_cout), .S(fa_1_s[6]), .Cout(fa_7_cout));
  FA fa_8 (.A(A[7]), .B(B[7]), .Cin(fa_7_cout), .S(fa_1_s[7]), .Cout(Cout));

  // Notes on the sheet:
  //   1607100
endmodule

// B
module B_Register (
  input  nLB,
  input  [7:0] INPUT,
  input  CLK,
  output [7:0] OUTPUT
);

  wire and_1_out, and_2_out, and_3_out, and_4_out, and_5_out, and_6_out, and_7_out, and_8_out, and_9_out,
       and_10_out, and_11_out, and_12_out, and_13_out, and_14_out, and_15_out, and_16_out, not_1_out,
       or_1_out, or_2_out, or_3_out, or_4_out, or_5_out, or_6_out, or_7_out, or_8_out;

  and and_1 (and_1_out, nLB, INPUT[7]);
  and and_2 (and_2_out, not_1_out, OUTPUT[7]);
  or or_1 (or_1_out, and_1_out, and_2_out);
  D_Flip_Flop d_ff_1 (.clk(CLK), .D(or_1_out), .Q(OUTPUT[7]));  // open: Qn, preset, en, reset
  and and_3 (and_3_out, not_1_out, OUTPUT[6]);
  and and_4 (and_4_out, nLB, INPUT[6]);
  or or_2 (or_2_out, and_4_out, and_3_out);
  D_Flip_Flop d_ff_2 (.clk(CLK), .D(or_2_out), .Q(OUTPUT[6]));  // open: Qn, preset, en, reset
  and and_5 (and_5_out, nLB, INPUT[5]);
  and and_6 (and_6_out, not_1_out, OUTPUT[5]);
  or or_3 (or_3_out, and_5_out, and_6_out);
  D_Flip_Flop d_ff_3 (.clk(CLK), .D(or_3_out), .Q(OUTPUT[5]));  // open: Qn, preset, en, reset
  and and_7 (and_7_out, nLB, INPUT[4]);
  and and_8 (and_8_out, not_1_out, OUTPUT[4]);
  or or_4 (or_4_out, and_7_out, and_8_out);
  D_Flip_Flop d_ff_4 (.clk(CLK), .D(or_4_out), .Q(OUTPUT[4]));  // open: Qn, preset, en, reset
  and and_9 (and_9_out, not_1_out, OUTPUT[3]);
  and and_10 (and_10_out, nLB, INPUT[3]);
  or or_5 (or_5_out, and_10_out, and_9_out);
  D_Flip_Flop d_ff_5 (.clk(CLK), .D(or_5_out), .Q(OUTPUT[3]));  // open: Qn, preset, en, reset
  and and_11 (and_11_out, nLB, INPUT[2]);
  or or_6 (or_6_out, and_11_out, and_12_out);
  and and_12 (and_12_out, not_1_out, OUTPUT[2]);
  D_Flip_Flop d_ff_6 (.clk(CLK), .D(or_6_out), .Q(OUTPUT[2]));  // open: Qn, preset, en, reset
  and and_13 (and_13_out, nLB, INPUT[1]);
  and and_14 (and_14_out, not_1_out, OUTPUT[1]);
  or or_7 (or_7_out, and_13_out, and_14_out);
  D_Flip_Flop d_ff_7 (.clk(CLK), .D(or_7_out), .Q(OUTPUT[1]));  // open: Qn, preset, en, reset
  not not_1 (not_1_out, nLB);
  and and_15 (and_15_out, not_1_out, OUTPUT[0]);
  and and_16 (and_16_out, nLB, INPUT[0]);
  or or_8 (or_8_out, and_16_out, and_15_out);
  D_Flip_Flop d_ff_8 (.clk(CLK), .D(or_8_out), .Q(OUTPUT[0]));  // open: Qn, preset, en, reset

  // Notes on the sheet:
  //   1607100
  //   B Register
endmodule

// O/P
module Output_Register (
  input  nLO,
  input  [7:0] INPUT,
  input  CLK,
  output [7:0] OUTPUT
);

  wire and_1_out, and_2_out, and_3_out, and_4_out, and_5_out, and_6_out, and_7_out, and_8_out, and_9_out,
       and_10_out, and_11_out, and_12_out, and_13_out, and_14_out, and_15_out, and_16_out, not_1_out,
       or_1_out, or_2_out, or_3_out, or_4_out, or_5_out, or_6_out, or_7_out, or_8_out;

  and and_1 (and_1_out, not_1_out, OUTPUT[7]);
  and and_2 (and_2_out, nLO, INPUT[7]);
  or or_1 (or_1_out, and_2_out, and_1_out);
  D_Flip_Flop d_ff_1 (.clk(CLK), .D(or_1_out), .Q(OUTPUT[7]));  // open: Qn, preset, en, reset
  and and_3 (and_3_out, not_1_out, OUTPUT[6]);
  and and_4 (and_4_out, nLO, INPUT[6]);
  or or_2 (or_2_out, and_4_out, and_3_out);
  D_Flip_Flop d_ff_2 (.clk(CLK), .D(or_2_out), .Q(OUTPUT[6]));  // open: Qn, preset, en, reset
  and and_5 (and_5_out, nLO, INPUT[5]);
  or or_3 (or_3_out, and_5_out, and_6_out);
  and and_6 (and_6_out, not_1_out, OUTPUT[5]);
  D_Flip_Flop d_ff_3 (.clk(CLK), .D(or_3_out), .Q(OUTPUT[5]));  // open: Qn, preset, en, reset
  and and_7 (and_7_out, nLO, INPUT[4]);
  or or_4 (or_4_out, and_7_out, and_8_out);
  and and_8 (and_8_out, not_1_out, OUTPUT[4]);
  D_Flip_Flop d_ff_4 (.clk(CLK), .D(or_4_out), .Q(OUTPUT[4]));  // open: Qn, preset, en, reset
  and and_9 (and_9_out, nLO, INPUT[3]);
  or or_5 (or_5_out, and_9_out, and_10_out);
  and and_10 (and_10_out, not_1_out, OUTPUT[3]);
  D_Flip_Flop d_ff_5 (.clk(CLK), .D(or_5_out), .Q(OUTPUT[3]));  // open: Qn, preset, en, reset
  and and_11 (and_11_out, nLO, INPUT[2]);
  and and_12 (and_12_out, not_1_out, OUTPUT[2]);
  or or_6 (or_6_out, and_11_out, and_12_out);
  D_Flip_Flop d_ff_6 (.clk(CLK), .D(or_6_out), .Q(OUTPUT[2]));  // open: Qn, preset, en, reset
  and and_13 (and_13_out, nLO, INPUT[1]);
  and and_14 (and_14_out, not_1_out, OUTPUT[1]);
  or or_7 (or_7_out, and_13_out, and_14_out);
  D_Flip_Flop d_ff_7 (.clk(CLK), .D(or_7_out), .Q(OUTPUT[1]));  // open: Qn, preset, en, reset
  and and_15 (and_15_out, nLO, INPUT[0]);
  and and_16 (and_16_out, not_1_out, OUTPUT[0]);
  or or_8 (or_8_out, and_15_out, and_16_out);
  not not_1 (not_1_out, nLO);
  D_Flip_Flop d_ff_8 (.clk(CLK), .D(or_8_out), .Q(OUTPUT[0]));  // open: Qn, preset, en, reset

  // Notes on the sheet:
  //   1607100
  //   Output Register
endmodule

// Counter
module ring_counter (
  input  CLK,
  input  CLR,
  output T6,
  output T5,
  output T4,
  output T3,
  output T2,
  output T1
);

  wire j_k_ff_1_qn, j_k_ff_2_qn, j_k_ff_3_qn, j_k_ff_4_qn, j_k_ff_5_qn, j_k_ff_6_q, not_1_out;

  J_K_Flip_Flop j_k_ff_1 (
    .J(T5), .clk(not_1_out), .K(j_k_ff_2_qn), .Q(T6), .Qn(j_k_ff_1_qn), .reset(CLR));  // open: preset, en
  J_K_Flip_Flop j_k_ff_2 (
    .J(T4), .clk(not_1_out), .K(j_k_ff_3_qn), .Q(T5), .Qn(j_k_ff_2_qn), .reset(CLR));  // open: preset, en
  J_K_Flip_Flop j_k_ff_3 (
    .J(T3), .clk(not_1_out), .K(j_k_ff_4_qn), .Q(T4), .Qn(j_k_ff_3_qn), .reset(CLR));  // open: preset, en
  J_K_Flip_Flop j_k_ff_4 (
    .J(T2), .clk(not_1_out), .K(j_k_ff_5_qn), .Q(T3), .Qn(j_k_ff_4_qn), .reset(CLR));  // open: preset, en
  J_K_Flip_Flop j_k_ff_5 (
    .J(T1), .clk(not_1_out), .K(j_k_ff_6_q), .Q(T2), .Qn(j_k_ff_5_qn), .reset(CLR));  // open: preset, en
  J_K_Flip_Flop j_k_ff_6 (
    .J(j_k_ff_1_qn), .clk(not_1_out), .K(T6), .Q(j_k_ff_6_q), .Qn(T1), .reset(CLR));  // open: preset, en
  not not_1 (not_1_out, CLK);

  // Notes on the sheet:
  //   1607061
endmodule

// Decoder
module decoder (
  input  I7,
  input  I6,
  input  I5,
  input  I4,
  output LDA,
  output ADD,
  output SUB,
  output OUT,
  output HLT
);

  wire and_1_out, and_2_out, and_3_out, and_4_out, not_1_out, not_2_out, not_3_out, not_4_out;

  not not_1 (not_1_out, I7);
  not not_2 (not_2_out, I6);
  not not_3 (not_3_out, I5);
  not not_4 (not_4_out, I4);
  and and_1 (and_1_out, not_1_out, not_2_out, not_3_out, not_4_out);
  and and_2 (and_2_out, not_1_out, not_2_out, not_3_out, I4);
  and and_3 (and_3_out, not_1_out, not_2_out, I5, not_4_out);
  and and_4 (and_4_out, I7, I6, I5, not_4_out);
  and and_5 (HLT, I7, I6, I5, I4);
  buf buffer_1 (LDA, and_1_out);
  buf buffer_2 (ADD, and_2_out);
  buf buffer_3 (SUB, and_3_out);
  buf buffer_4 (OUT, and_4_out);

  // Notes on the sheet:
  //   1607061
endmodule

module Controller_Sequencer (
  input  [3:0] I7_I4,
  input  CLR,
  input  CLK,
  output HLT,
  output CP,
  output EP,
  output nLM,
  output nCE,
  output nLI,
  output nEI,
  output nLA,
  output EA,
  output SU,
  output EU,
  output nLB,
  output nLO
);

  wire and_1_out, and_2_out, and_3_out, and_4_out, and_5_out, and_6_out, and_7_out, and_8_out, and_9_out,
       and_10_out, and_11_out, and_12_out, and_15_out, and_16_out, and_17_out, and_18_out, decoder_1_add,
       decoder_1_lda, decoder_1_out, decoder_1_sub, or_1_out, or_2_out, or_3_out, or_4_out, or_6_out,
       ring_counter_1_t3, ring_counter_1_t4, ring_counter_1_t5, ring_counter_1_t6;

  decoder decoder_1 (
    .I7(I7_I4[3]), .I6(I7_I4[2]), .I5(I7_I4[1]), .I4(I7_I4[0]), .LDA(decoder_1_lda), .ADD(decoder_1_add),
    .SUB(decoder_1_sub), .OUT(decoder_1_out), .HLT(HLT));
  and and_1 (and_1_out, decoder_1_lda, ring_counter_1_t4);
  and and_2 (and_2_out, decoder_1_add, ring_counter_1_t4);
  or or_1 (or_1_out, EP, and_1_out, and_2_out, and_3_out);
  not not_1 (nLM, or_1_out);
  and and_3 (and_3_out, decoder_1_sub, ring_counter_1_t4);
  and and_4 (and_4_out, decoder_1_add, ring_counter_1_t5);
  and and_5 (and_5_out, decoder_1_lda, ring_counter_1_t5);
  or or_2 (or_2_out, ring_counter_1_t3, and_5_out, and_4_out, and_6_out);
  not not_2 (nCE, or_2_out);
  and and_6 (and_6_out, decoder_1_sub, ring_counter_1_t5);
  not not_3 (nLI, ring_counter_1_t3);
  and and_7 (and_7_out, decoder_1_lda, ring_counter_1_t4);
  and and_8 (and_8_out, decoder_1_add, ring_counter_1_t4);
  or or_3 (or_3_out, and_7_out, and_8_out, and_9_out);
  not not_4 (nEI, or_3_out);
  ring_counter ring_counter_1 (
    .CLR(CLR), .T6(ring_counter_1_t6), .T5(ring_counter_1_t5), .T4(ring_counter_1_t4),
    .T3(ring_counter_1_t3), .T2(CP), .T1(EP), .CLK(CLK));
  and and_9 (and_9_out, decoder_1_sub, ring_counter_1_t4);
  and and_10 (and_10_out, decoder_1_add, ring_counter_1_t6);
  and and_11 (and_11_out, decoder_1_lda, ring_counter_1_t5);
  or or_4 (or_4_out, and_11_out, and_10_out, and_12_out);
  not not_5 (nLA, or_4_out);
  and and_12 (and_12_out, decoder_1_sub, ring_counter_1_t6);
  and and_13 (SU, decoder_1_sub, ring_counter_1_t6);
  and and_14 (EA, decoder_1_out, ring_counter_1_t4);
  and and_15 (and_15_out, decoder_1_add, ring_counter_1_t6);
  and and_16 (and_16_out, decoder_1_sub, ring_counter_1_t6);
  or or_5 (EU, and_15_out, and_16_out);
  and and_17 (and_17_out, decoder_1_sub, ring_counter_1_t5);
  and and_18 (and_18_out, decoder_1_add, ring_counter_1_t5);
  or or_6 (or_6_out, and_18_out, and_17_out);
  not not_6 (nLB, or_6_out);
  nand nand_1 (nLO, decoder_1_out, ring_counter_1_t4);

  // Notes on the sheet:
  //   1607061 & 1607100
  //   LDA
  //   ADD
  //   SUB
  //   OUT
endmodule

// 4-bit-register
module register_4bit (
  input  Load,
  input  x3,
  input  x2,
  input  x1,
  input  x0,
  input  CLK,
  input  CL,
  input  EN,
  output y3,
  output y2,
  output y1,
  output y0
);

  wire and_1_out, and_2_out, and_3_out, and_4_out, and_5_out, and_6_out, and_7_out, and_8_out, d_ff_1_q,
       d_ff_2_q, d_ff_3_q, d_ff_4_q, not_1_out, or_1_out, or_2_out, or_3_out, or_4_out;

  and and_1 (and_1_out, d_ff_1_q, not_1_out);
  and and_2 (and_2_out, x3, Load);
  or or_1 (or_1_out, and_1_out, and_2_out);
  D_Flip_Flop d_ff_1 (.clk(CLK), .D(or_1_out), .Q(d_ff_1_q), .reset(CL));  // open: Qn, preset, en
  assign y3 = EN ? d_ff_1_q : 1'bz;  // Controlled_Buffer controlled_buffer_1
  and and_3 (and_3_out, d_ff_2_q, not_1_out);
  and and_4 (and_4_out, x2, Load);
  or or_2 (or_2_out, and_3_out, and_4_out);
  D_Flip_Flop d_ff_2 (.clk(CLK), .D(or_2_out), .Q(d_ff_2_q), .reset(CL));  // open: Qn, preset, en
  assign y2 = EN ? d_ff_2_q : 1'bz;  // Controlled_Buffer controlled_buffer_2
  and and_5 (and_5_out, d_ff_3_q, not_1_out);
  or or_3 (or_3_out, and_5_out, and_6_out);
  and and_6 (and_6_out, x1, Load);
  D_Flip_Flop d_ff_3 (.clk(CLK), .D(or_3_out), .Q(d_ff_3_q), .reset(CL));  // open: Qn, preset, en
  assign y1 = EN ? d_ff_3_q : 1'bz;  // Controlled_Buffer controlled_buffer_3
  and and_7 (and_7_out, d_ff_4_q, not_1_out);
  and and_8 (and_8_out, x0, Load);
  or or_4 (or_4_out, and_7_out, and_8_out);
  not not_1 (not_1_out, Load);
  D_Flip_Flop d_ff_4 (.clk(CLK), .D(or_4_out), .Q(d_ff_4_q), .reset(CL));  // open: Qn, preset, en
  assign y0 = EN ? d_ff_4_q : 1'bz;  // Controlled_Buffer controlled_buffer_4

  // Notes on the sheet:
  //   1607061
endmodule

module IR (
  input  LOAD,
  input  CLK,
  input  [7:0] INPUT,
  input  ENABLE,
  input  CLR,
  output [3:0] OUTPUT0_3,
  output [3:0] OUTPUT4_7
);

  register_4bit register_4bit_1 (
    .x3(INPUT[7]), .x2(INPUT[6]), .x1(INPUT[5]), .x0(INPUT[4]), .Load(LOAD), .CLK(CLK), .CL(CLR),
    .EN(ENABLE), .y3(OUTPUT4_7[3]), .y2(OUTPUT4_7[2]), .y1(OUTPUT4_7[1]), .y0(OUTPUT4_7[0]));
  register_4bit register_4bit_2 (
    .x3(INPUT[3]), .x2(INPUT[2]), .x1(INPUT[1]), .x0(INPUT[0]), .Load(LOAD), .CLK(CLK), .CL(CLR),
    .EN(ENABLE), .y3(OUTPUT0_3[3]), .y2(OUTPUT0_3[2]), .y1(OUTPUT0_3[1]), .y0(OUTPUT0_3[0]));

  // Notes on the sheet:
  //   1607061
endmodule

// MAR
module mar (
  input  [3:0] INPUT,
  input  LOAD,
  input  CLK,
  input  CLR,
  input  ENABLE,
  output [3:0] OUTPUT
);

  wire and_1_out, and_2_out, and_3_out, and_4_out, and_5_out, and_6_out, and_7_out, and_8_out, d_ff_1_q,
       d_ff_2_q, d_ff_3_q, d_ff_4_q, not_1_out, or_1_out, or_2_out, or_3_out, or_4_out;

  and and_1 (and_1_out, d_ff_1_q, not_1_out);
  or or_1 (or_1_out, and_1_out, and_2_out);
  and and_2 (and_2_out, INPUT[3], LOAD);
  D_Flip_Flop d_ff_1 (.clk(CLK), .D(or_1_out), .Q(d_ff_1_q), .reset(CLR));  // open: Qn, preset, en
  assign OUTPUT[3] = ENABLE ? d_ff_1_q : 1'bz;  // Controlled_Buffer controlled_buffer_1
  and and_3 (and_3_out, d_ff_2_q, not_1_out);
  or or_2 (or_2_out, and_3_out, and_4_out);
  D_Flip_Flop d_ff_2 (.clk(CLK), .D(or_2_out), .Q(d_ff_2_q), .reset(CLR));  // open: Qn, preset, en
  assign OUTPUT[2] = ENABLE ? d_ff_2_q : 1'bz;  // Controlled_Buffer controlled_buffer_2
  and and_4 (and_4_out, INPUT[2], LOAD);
  and and_5 (and_5_out, d_ff_3_q, not_1_out);
  or or_3 (or_3_out, and_5_out, and_6_out);
  D_Flip_Flop d_ff_3 (.clk(CLK), .D(or_3_out), .Q(d_ff_3_q), .reset(CLR));  // open: Qn, preset, en
  and and_6 (and_6_out, INPUT[1], LOAD);
  assign OUTPUT[1] = ENABLE ? d_ff_3_q : 1'bz;  // Controlled_Buffer controlled_buffer_3
  and and_7 (and_7_out, d_ff_4_q, not_1_out);
  not not_1 (not_1_out, LOAD);
  and and_8 (and_8_out, INPUT[0], LOAD);
  or or_4 (or_4_out, and_7_out, and_8_out);
  D_Flip_Flop d_ff_4 (.clk(CLK), .D(or_4_out), .Q(d_ff_4_q), .reset(CLR));  // open: Qn, preset, en
  assign OUTPUT[0] = ENABLE ? d_ff_4_q : 1'bz;  // Controlled_Buffer controlled_buffer_4

  // Notes on the sheet:
  //   1607061
endmodule

module instruction_register (
  input  I7,
  input  I6,
  input  I5,
  input  I4,
  output LDA,
  output ADD,
  output SUB,
  output OUT,
  output HLT
);

  wire not_1_out, not_2_out, not_3_out, not_4_out;

  not not_1 (not_1_out, I7);
  not not_2 (not_2_out, I6);
  not not_3 (not_3_out, I5);
  not not_4 (not_4_out, I4);
  and and_1 (LDA, I7, not_2_out, I5, I4);
  and and_2 (ADD, not_1_out, I6, not_3_out, I4);
  and and_3 (SUB, not_1_out, I6, I5, I4);
  and and_4 (OUT, not_1_out, not_2_out, not_3_out, not_4_out);
  and and_5 (HLT, not_1_out, I6, not_3_out, not_4_out);

  // Notes on the sheet:
  //   1607061
endmodule

// PC
module pc (
  input  Cp,
  input  CLK,
  input  CLR,
  input  Ep,
  output [3:0] Output
);

  wire j_k_ff_1_q, j_k_ff_2_q, j_k_ff_3_q, j_k_ff_4_q, not_1_out, not_2_out, not_3_out, not_4_out;

  assign Output[3] = Ep ? j_k_ff_1_q : 1'bz;  // Controlled_Buffer controlled_buffer_1
  assign Output[2] = Ep ? j_k_ff_2_q : 1'bz;  // Controlled_Buffer controlled_buffer_2
  not not_1 (not_1_out, j_k_ff_2_q);
  J_K_Flip_Flop j_k_ff_1 (.J(Cp), .clk(not_1_out), .K(Cp), .Q(j_k_ff_1_q), .reset(CLR));  // open: Qn, preset, en
  assign Output[1] = Ep ? j_k_ff_3_q : 1'bz;  // Controlled_Buffer controlled_buffer_3
  not not_2 (not_2_out, j_k_ff_3_q);
  J_K_Flip_Flop j_k_ff_2 (.J(Cp), .clk(not_2_out), .K(Cp), .Q(j_k_ff_2_q), .reset(CLR));  // open: Qn, preset, en
  assign Output[0] = Ep ? j_k_ff_4_q : 1'bz;  // Controlled_Buffer controlled_buffer_4
  not not_3 (not_3_out, j_k_ff_4_q);
  J_K_Flip_Flop j_k_ff_3 (.J(Cp), .clk(not_3_out), .K(Cp), .Q(j_k_ff_3_q), .reset(CLR));  // open: Qn, preset, en
  J_K_Flip_Flop j_k_ff_4 (.J(Cp), .clk(not_4_out), .K(Cp), .Q(j_k_ff_4_q), .reset(CLR));  // open: Qn, preset, en
  not not_4 (not_4_out, CLK);

  // Notes on the sheet:
  //   1607061
endmodule
